# Fritzing sketch schematic (saved by Fritzing 0.9.6b)

parts:
  Part2 = Arduino Nano (Rev3.0)
  U1 = MAX485 [package=dil08]
  XLR2 = XLR3_NCFAH2 [package=xlr3_nc3fah2]
  Part3 = ws2812b [package="smd 2812b"]
  S3 = Toggle Switch [package=THT]

nets:
  N1: Part2.D0/RX, U1.RO
  GND: Part2.GND, U1.RE, U1.DE, U1.GND, XLR2.1, XLR2.G
  N2: Part2.D6, Part3.DIN
  N3: Part2.D9, S3.L1
  N4: Part2.D10, S3.L2
  5V: Part2.5V, U1.VCC, S3.COM
  N5: U1.A, XLR2.3
  N6: U1.B, XLR2.2
